# Fritzing sketch Untitled Sketch (saved by Fritzing 0.9.3b)
breadboards: 1

parts:
  Raspberry_Pi_1 = Raspberry Pi 3 [part_number=RPI-3-V1.2]
  S1 = Round Pushbutton
  R1 = Resistor [tolerance=±0.05% resistance=10k package="1206 [SMD]"]
  R2 = Resistor [tolerance=±5% resistance=220 package=THT]
  LED1 = LED - 5mm [color="Red (633nm)" package="5 mm [THT]"]

nets:
  N1: Raspberry_Pi_1.3v3, S1.leg0
  N2: Raspberry_Pi_1.GIPO18, R1.Pin_1
  N3: Raspberry_Pi_1.GIPO15, LED1.anode
  N4: Raspberry_Pi_1.GND, R2.Pin_1
  N5: S1.leg1, R1.Pin_0
  N6: R2.Pin_0, LED1.cathode
